# Fritzing sketch FONA_Location (saved by Fritzing 0.9.1b)
breadboards: 1

parts:
  Parte1 = Arduino Uno (Rev3)
  Parte2 = Adafruit FONA - Mini Cellular GSM Breakout
  BATT1 = LiPoly Battery (1300mAh)

nets:
  N1: Parte1.D3_PWM, Parte2.RXD_5V
  N2: Parte1.D4, Parte2.TXD_5V
  N3: Parte1.D6_PWM, Parte2.PWRSTAT_5V
  N4: Parte1.D7, Parte2.PWRKEY_5V
  N5: Parte1.5V, Parte2.VCCIO
  N6: Parte1.GND, Parte2.GND#106
  N7: Parte2.GND#55, BATT1.positive, BATT1.negative

notes:
  connect antenna here

custom parts:
  Adafruit FONA - Mini Cellular GSM Breakout: An all-in-one cellular phone module that lets you add voice, text, SMS and GPRS data to your project. Quad-band 850/900/1800/1900MHz - connect onto any global GSM network with any 2G SIM. Includes an onboard LiPoly battery charging circuitry so you can take your project on the go. Also works as an FM radio receiver.
  LiPoly Battery (1300mAh): Lithium Ion Polymer Battery (1300mAh)
