# Fritzing sketch GPS_SDWriting (saved by Fritzing 0.9.1b)
breadboards: 1

parts:
  Parte1 = Arduino Uno (Rev3)
  GPS1 = Adafruit Ultimate GPS Breakout
  microSD1 = MicroSD Breakout

nets:
  N1: Parte1.D10_PWM/SS, microSD1.CS
  N2: Parte1.D11_PWM/MOSI, microSD1.DI
  N3: Parte1.D12/MISO, microSD1.DO
  N4: Parte1.D13/SCK, microSD1.CLK
  N5: Parte1.D2, GPS1.RX
  N6: Parte1.D3_PWM, GPS1.TX
  3V3: Parte1.3V3, GPS1.3.3V
  5V: Parte1.5V, microSD1.5V
  GND: Parte1.GND, GPS1.GND, microSD1.GND

custom parts:
  MicroSD Breakout: 5V-ready microSD Breakout with Level Shifter
