# Fritzing sketch WifiWebClientRepeating_TempLightSensors (saved by Fritzing 0.9.1b)
breadboards: 1

parts:
  Parte1 = Arduino Uno (Rev3)
  R1 = Resistor [tolerance=±5% resistance=10k package=THT]
  R2 = Photocell (LDR) [package=THT]
  T1 = LM35 Temperature Sensor [package="TO92 [THT]"]

nets:
  N1: Parte1.A0, T1.Vout
  N2: Parte1.A1, R1.Pin_1, R2.pin_0
  N3: Parte1.5V, R2.pin_1, T1.+Vs
  GND: Parte1.GND, R1.Pin_0, T1.GND

notes:
  Plug WiFi Shield on Arduino
